# Fritzing sketch DuinoMultiRemote (saved by Fritzing 0.9.2b)
breadboards: 2

parts:
  Composant1 = Arduino Uno (Rev3)
  S1 = Momentary Switch [package=ksa_sealed_tac_switch]
  R2 = Resistor [tolerance=±5% resistance=1k package=THT]
  R4 = Resistor [tolerance=±5% resistance=1k package=THT]
  U2 = POT [package=pot_alpha_rv16af-20]  # not connected
  LED2 = RGB LED - (4 legs) [package="5 mm [THT]"]
  R5 = Resistor [tolerance=±5% resistance=260 package=THT]
  R6 = Resistor [tolerance=±5% resistance=260 package=THT]
  R7 = Resistor [tolerance=±5% resistance=260 package=THT]
  LED3 = LED - 5mm [color="Red (633nm)" package="5 mm [THT]"]
  U4 = POT [package=pot_alpha_rv16af-20]  # not connected
  U3 = LCD-16X2 [package=lcd-8x2-kit]  # not connected
  U3_2 = LCD-16X2 [package=lcd-16x2_noholes]

nets:
  N1: Composant1.D8, U3_2.E
  N2: Composant1.D9_PWM, R7.Pin_1
  N3: Composant1.D10_PWM/SS, U3_2.DB4
  N4: Composant1.D11_PWM/MOSI, U3_2.DB5
  N5: Composant1.D12/MISO, U3_2.DB6
  N6: Composant1.D13/SCK, U3_2.DB7
  N7: Composant1.D2, S1.4
  N8: Composant1.D3_PWM, R2.Pin_1
  N9: Composant1.D5_PWM, R5.Pin_1
  N10: Composant1.D6_PWM, R6.Pin_1
  N11: Composant1.D7, U3_2.RS
  5V: Composant1.5V, S1.2, U3_2.VDD, U3_2.A
  GND: Composant1.GND, R4.Pin_1, LED2.green_cathode, LED3.anode, U3_2.VSS, U3_2.R_W, U3_2.K
  N12: R2.Pin_0, LED3.cathode
  N13: LED2.red_cathode, R5.Pin_0
  N14: LED2.common_anode, R6.Pin_0
  N15: LED2.blue_cathode, R7.Pin_0
